# Fritzing sketch fritizing (saved by Fritzing 0.9.3b)
circuit board: 6.23919cm x 5.92222cm

parts:
  Part1 = Adafruit TSL2561 [part_number="Adafruit #439"]
  gp20u7 = Raspberry Pi 3 [part_number=RPI-3-V1.2]
  Part2 = Adafruit LIS3DH [part_number="Adafruit #2809"]

nets:
  VIN: Part1.VIN, Part1.ADDR, gp20u7.3v3, gp20u7.3V3, Part2.VIN
  GND: Part1.GND, gp20u7.GND, Part2.GND
  N1: Part1.SDA, gp20u7.GPIO2, Part2.SDA
  N2: Part1.SCL, gp20u7.GPIO3, Part2.SCL
  N3: gp20u7.GPIO6, Part2.INT1

notes:
  ET-Collar

custom parts:
  Adafruit TSL2561: The TSL2561 luminosity sensor is an advanced digital light sensor, ideal for use in a wide range of light situations. Compared to low cost CdS cells, this sensor is more precise, allowing for exact lux calculations and can be configured for different gain/timing ranges to detect light ranges from up to 0.1 - 40,000+ Lux on the fly. The best part of this sensor is that it contains both infrared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
  Adafruit LIS3DH: The LIS3DH is a very popular low power triple-axis accelerometer. It's low-cost, but has just about every 'extra' you'd want in an accelerometer: Three axis sensing, 10-bit precision ±2g/±4g/±8g/±16g selectable scaling Both I2C (2 possible addresses) and SPI interface options Interrupt output Multiple data rate options 1 Hz to 5Khz As low as 2uA current draw (just the chip itself, not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
